# Fritzing sketch Circuit (saved by Fritzing 0.9.3b)

parts:
  J1 = Piezo Speaker
  Part1 = Arduino Uno (Rev3)

nets:
  N1: J1.pin1, Part1.GND
  N2: J1.pin2, Part1.D11_PWM/MOSI

notes:
  G  R  Y    Infared Reciever

// code stored in the sketch: IR.ino
#include <IRremote.h>
//Thisis the Reciever module for the SteamAlexaKey Python Project
const int RECV_PIN = 6;

IRrecv irrecv(RECV_PIN);

decode_results results;

void setup()
{
  Serial.begin(9600);
  irrecv.enableIRIn(); // Start the receiver
  irrecv.blink13(true);
}

void loop() {
  if (irrecv.decode(&results)) {
    if (results.decode_type == NEC) {
      Serial.print("NEC: ");
    } else if (results.decode_type == SONY) {
      Serial.print("SONY: ");
    } else if (results.decode_type == RC5) {
      Serial.print("RC5: ");
    } else if (results.decode_type == RC6) {
      Serial.print("RC6: ");
    } else if (results.decode_type == UNKNOWN) {
      Serial.print("UNKNOWN: ");
    }
    Serial.println(results.value, HEX);
    irrecv.resume(); // Receive the next value
  }
}
